// Logisim project 16bit.circ as structural Verilog: 2 circuits, main circuit main
module main (
  input  i0,
  input  i1,
  input  i2,
  input  i3,
  input  i4,
  input  i5,
  input  i6,
  input  i7,
  input  i8,
  input  i9,
  input  i10,
  input  i11,
  input  i12,
  input  i13,
  input  i14,
  input  i15,
  input  [1:0] FunSel,
  input  Enable,
  output out0,
  output out1,
  output out2,
  output out3,
  output out4,
  output out5,
  output out6,
  output out7,
  output out8,
  output out9,
  output out10,
  output out11,
  output out12,
  output out13,
  output out14,
  output out15
);

  wire CLK_out;

  Clock CLK (.out(CLK_out));
  Hex_Digit_Display hex_digit_display_1 (.value({i15, i14, i13, i12}));  // open: dp
  Hex_Digit_Display hex_digit_display_2 (.value({i11, i10, i9, i8}));  // open: dp
  Hex_Digit_Display hex_digit_display_3 (.value({i7, i6, i5, i4}));  // open: dp
  Hex_Digit_Display hex_digit_display_4 (.value({i3, i2, i1, i0}));  // open: dp
  _16bit u_16bit_1 (
    .FunSel(FunSel), .CLK(CLK_out), .Enable(Enable), .i0(i0), .i1(i1), .i2(i2), .i3(i3), .i4(i4), .i5(i5),
    .i6(i6), .i7(i7), .i8(i8), .i9(i9), .i10(i10), .i11(i11), .i12(i12), .i13(i13), .i14(i14), .i15(i15),
    .out0(out0), .out1(out1), .out2(out2), .out3(out3), .out4(out4), .out5(out5), .out6(out6), .out7(out7),
    .out8(out8), .out9(out9), .out10(out10), .out11(out11), .out12(out12), .out13(out13), .out14(out14),
    .out15(out15));
  Hex_Digit_Display hex_digit_display_5 (.value({out15, out14, out13, out12}));  // open: dp
  Hex_Digit_Display hex_digit_display_6 (.value({out11, out10, out9, out8}));  // open: dp
  Hex_Digit_Display hex_digit_display_7 (.value({out7, out6, out5, out4}));  // open: dp
  Hex_Digit_Display hex_digit_display_8 (.value({out3, out2, out1, out0}));  // open: dp
endmodule

module _16bit (
  input  i0,
  input  i1,
  input  i2,
  input  i3,
  input  i4,
  input  i5,
  input  i6,
  input  i7,
  input  i8,
  input  i9,
  input  i10,
  input  i11,
  input  i12,
  input  i13,
  input  i14,
  input  i15,
  input  [1:0] FunSel,
  input  CLK,
  input  Enable,
  output out0,
  output out1,
  output out2,
  output out3,
  output out4,
  output out5,
  output out6,
  output out7,
  output out8,
  output out9,
  output out10,
  output out11,
  output out12,
  output out13,
  output out14,
  output out15
);

  wire adder_1_cout, adder_1_out, adder_2_cout, adder_2_out, adder_3_cout, adder_3_out, adder_4_cout,
       adder_4_out, adder_5_cout, adder_5_out, adder_6_cout, adder_6_out, adder_7_cout, adder_7_out,
       adder_8_cout, adder_8_out, adder_9_cout, adder_9_out, adder_10_cout, adder_10_out, adder_11_cout,
       adder_11_out, adder_12_cout, adder_12_out, adder_13_cout, adder_13_out, adder_14_cout, adder_14_out,
       adder_15_cout, adder_15_out, adder_16_out, multiplexer_1_out, multiplexer_2_out, multiplexer_3_out,
       multiplexer_4_out, multiplexer_5_out, multiplexer_6_out, multiplexer_7_out, multiplexer_8_out,
       multiplexer_9_out, multiplexer_10_out, multiplexer_11_out, multiplexer_12_out, multiplexer_13_out,
       multiplexer_14_out, multiplexer_15_out, multiplexer_16_out, not_1_out, not_2_out, subtractor_1_bout,
       subtractor_1_out, subtractor_2_bout, subtractor_2_out, subtractor_3_bout, subtractor_3_out,
       subtractor_4_bout, subtractor_4_out, subtractor_5_bout, subtractor_5_out, subtractor_6_bout,
       subtractor_6_out, subtractor_7_bout, subtractor_7_out, subtractor_8_bout, subtractor_8_out,
       subtractor_9_bout, subtractor_9_out, subtractor_10_bout, subtractor_10_out, subtractor_11_bout,
       subtractor_11_out, subtractor_12_bout, subtractor_12_out, subtractor_13_bout, subtractor_13_out,
       subtractor_14_bout, subtractor_14_out, subtractor_15_bout, subtractor_15_out, subtractor_16_out;

  Multiplexer #(.select(2), .enable("false")) multiplexer_1 (
    .in0(not_1_out), .in1(i0), .in2(adder_1_out), .in3(subtractor_1_out), .out(multiplexer_1_out),
    .sel(FunSel));
  not not_1 (not_1_out, Enable);
  Adder #(.width(1)) adder_1 (.a(out0), .b(Enable), .out(adder_1_out), .cout(adder_1_cout));  // open: cin
  Subtractor #(.width(1)) subtractor_1 (
    .a(out0), .b(Enable), .out(subtractor_1_out), .bout(subtractor_1_bout));  // open: bin
  D_Flip_Flop d_ff_1 (.clk(CLK), .D(multiplexer_1_out), .Q(out0), .en(Enable));  // open: Qn, preset, reset
  Multiplexer #(.select(2), .enable("false")) multiplexer_2 (
    .in0(not_1_out), .in1(i1), .in2(adder_2_out), .in3(subtractor_2_out), .out(multiplexer_2_out),
    .sel(FunSel));
  D_Flip_Flop d_ff_2 (.clk(CLK), .D(multiplexer_2_out), .Q(out1), .en(Enable));  // open: Qn, preset, reset
  Adder #(.width(1)) adder_2 (.a(out1), .b(adder_1_cout), .out(adder_2_out), .cout(adder_2_cout));  // open: cin
  Subtractor #(.width(1)) subtractor_2 (
    .a(out1), .b(subtractor_1_bout), .out(subtractor_2_out), .bout(subtractor_2_bout));  // open: bin
  Multiplexer #(.select(2), .enable("false")) multiplexer_3 (
    .in0(not_1_out), .in1(i2), .in2(adder_3_out), .in3(subtractor_3_out), .out(multiplexer_3_out),
    .sel(FunSel));
  D_Flip_Flop d_ff_3 (.clk(CLK), .D(multiplexer_3_out), .Q(out2), .en(Enable));  // open: Qn, preset, reset
  Adder #(.width(1)) adder_3 (.a(out2), .b(adder_2_cout), .out(adder_3_out), .cout(adder_3_cout));  // open: cin
  Subtractor #(.width(1)) subtractor_3 (
    .a(out2), .b(subtractor_2_bout), .out(subtractor_3_out), .bout(subtractor_3_bout));  // open: bin
  Multiplexer #(.select(2), .enable("false")) multiplexer_4 (
    .in0(not_1_out), .in1(i3), .in2(adder_4_out), .in3(subtractor_4_out), .out(multiplexer_4_out),
    .sel(FunSel));
  D_Flip_Flop d_ff_4 (.clk(CLK), .D(multiplexer_4_out), .Q(out3), .en(Enable));  // open: Qn, preset, reset
  Adder #(.width(1)) adder_4 (.a(out3), .b(adder_3_cout), .out(adder_4_out), .cout(adder_4_cout));  // open: cin
  Subtractor #(.width(1)) subtractor_4 (
    .a(out3), .b(subtractor_3_bout), .out(subtractor_4_out), .bout(subtractor_4_bout));  // open: bin
  Multiplexer #(.select(2), .enable("false")) multiplexer_5 (
    .in0(not_1_out), .in1(i4), .in2(adder_5_out), .in3(subtractor_5_out), .out(multiplexer_5_out),
    .sel(FunSel));
  D_Flip_Flop d_ff_5 (.clk(CLK), .D(multiplexer_5_out), .Q(out4), .en(Enable));  // open: Qn, preset, reset
  Adder #(.width(1)) adder_5 (.a(out4), .b(adder_4_cout), .out(adder_5_out), .cout(adder_5_cout));  // open: cin
  Subtractor #(.width(1)) subtractor_5 (
    .a(out4), .b(subtractor_4_bout), .out(subtractor_5_out), .bout(subtractor_5_bout));  // open: bin
  Multiplexer #(.select(2), .enable("false")) multiplexer_6 (
    .in0(not_1_out), .in1(i5), .in2(adder_6_out), .in3(subtractor_6_out), .out(multiplexer_6_out),
    .sel(FunSel));
  D_Flip_Flop d_ff_6 (.clk(CLK), .D(multiplexer_6_out), .Q(out5), .en(Enable));  // open: Qn, preset, reset
  Adder #(.width(1)) adder_6 (.a(out5), .b(adder_5_cout), .out(adder_6_out), .cout(adder_6_cout));  // open: cin
  Subtractor #(.width(1)) subtractor_6 (
    .a(out5), .b(subtractor_5_bout), .out(subtractor_6_out), .bout(subtractor_6_bout));  // open: bin
  Multiplexer #(.select(2), .enable("false")) multiplexer_7 (
    .in0(not_1_out), .in1(i6), .in2(adder_7_out), .in3(subtractor_7_out), .out(multiplexer_7_out),
    .sel(FunSel));
  D_Flip_Flop d_ff_7 (.clk(CLK), .D(multiplexer_7_out), .Q(out6), .en(Enable));  // open: Qn, preset, reset
  Adder #(.width(1)) adder_7 (.a(out6), .b(adder_6_cout), .out(adder_7_out), .cout(adder_7_cout));  // open: cin
  Subtractor #(.width(1)) subtractor_7 (
    .a(out6), .b(subtractor_6_bout), .out(subtractor_7_out), .bout(subtractor_7_bout));  // open: bin
  Multiplexer #(.select(2), .enable("false")) multiplexer_8 (
    .in0(not_1_out), .in1(i7), .in2(adder_8_out), .in3(subtractor_8_out), .out(multiplexer_8_out),
    .sel(FunSel));
  D_Flip_Flop d_ff_8 (.clk(CLK), .D(multiplexer_8_out), .Q(out7), .en(Enable));  // open: Qn, preset, reset
  Adder #(.width(1)) adder_8 (.a(out7), .b(adder_7_cout), .out(adder_8_out), .cout(adder_8_cout));  // open: cin
  Subtractor #(.width(1)) subtractor_8 (
    .a(out7), .b(subtractor_7_bout), .out(subtractor_8_out), .bout(subtractor_8_bout));  // open: bin
  not not_2 (not_2_out, Enable);
  Multiplexer #(.select(2), .enable("false")) multiplexer_9 (
    .in0(not_2_out), .in1(i8), .in2(adder_9_out), .in3(subtractor_9_out), .out(multiplexer_9_out),
    .sel(FunSel));
  D_Flip_Flop d_ff_9 (.clk(CLK), .D(multiplexer_9_out), .Q(out8), .en(Enable));  // open: Qn, preset, reset
  Adder #(.width(1)) adder_9 (.a(out8), .b(adder_8_cout), .out(adder_9_out), .cout(adder_9_cout));  // open: cin
  Subtractor #(.width(1)) subtractor_9 (
    .a(out8), .b(subtractor_8_bout), .out(subtractor_9_out), .bout(subtractor_9_bout));  // open: bin
  Multiplexer #(.select(2), .enable("false")) multiplexer_10 (
    .in0(not_2_out), .in1(i9), .in2(adder_10_out), .in3(subtractor_10_out), .out(multiplexer_10_out),
    .sel(FunSel));
  D_Flip_Flop d_ff_10 (.clk(CLK), .D(multiplexer_10_out), .Q(out9), .en(Enable));  // open: Qn, preset, reset
  Adder #(.width(1)) adder_10 (.a(out9), .b(adder_9_cout), .out(adder_10_out), .cout(adder_10_cout));  // open: cin
  Subtractor #(.width(1)) subtractor_10 (
    .a(out9), .b(subtractor_9_bout), .out(subtractor_10_out), .bout(subtractor_10_bout));  // open: bin
  Multiplexer #(.select(2), .enable("false")) multiplexer_11 (
    .in0(not_2_out), .in1(i10), .in2(adder_11_out), .in3(subtractor_11_out), .out(multiplexer_11_out),
    .sel(FunSel));
  D_Flip_Flop d_ff_11 (.clk(CLK), .D(multiplexer_11_out), .Q(out10), .en(Enable));  // open: Qn, preset, reset
  Adder #(.width(1)) adder_11 (.a(out10), .b(adder_10_cout), .out(adder_11_out), .cout(adder_11_cout));  // open: cin
  Subtractor #(.width(1)) subtractor_11 (
    .a(out10), .b(subtractor_10_bout), .out(subtractor_11_out), .bout(subtractor_11_bout));  // open: bin
  Multiplexer #(.select(2), .enable("false")) multiplexer_12 (
    .in0(not_2_out), .in1(i11), .in2(adder_12_out), .in3(subtractor_12_out), .out(multiplexer_12_out),
    .sel(FunSel));
  D_Flip_Flop d_ff_12 (.clk(CLK), .D(multiplexer_12_out), .Q(out11), .en(Enable));  // open: Qn, preset, reset
  Adder #(.width(1)) adder_12 (.a(out11), .b(adder_11_cout), .out(adder_12_out), .cout(adder_12_cout));  // open: cin
  Subtractor #(.width(1)) subtractor_12 (
    .a(out11), .b(subtractor_11_bout), .out(subtractor_12_out), .bout(subtractor_12_bout));  // open: bin
  Multiplexer #(.select(2), .enable("false")) multiplexer_13 (
    .in0(not_2_out), .in1(i12), .in2(adder_13_out), .in3(subtractor_13_out), .out(multiplexer_13_out),
    .sel(FunSel));
  D_Flip_Flop d_ff_13 (.clk(CLK), .D(multiplexer_13_out), .Q(out12), .en(Enable));  // open: Qn, preset, reset
  Adder #(.width(1)) adder_13 (.a(out12), .b(adder_12_cout), .out(adder_13_out), .cout(adder_13_cout));  // open: cin
  Subtractor #(.width(1)) subtractor_13 (
    .a(out12), .b(subtractor_12_bout), .out(subtractor_13_out), .bout(subtractor_13_bout));  // open: bin
  Multiplexer #(.select(2), .enable("false")) multiplexer_14 (
    .in0(not_2_out), .in1(i13), .in2(adder_14_out), .in3(subtractor_14_out), .out(multiplexer_14_out),
    .sel(FunSel));
  D_Flip_Flop d_ff_14 (.clk(CLK), .D(multiplexer_14_out), .Q(out13), .en(Enable));  // open: Qn, preset, reset
  Adder #(.width(1)) adder_14 (.a(out13), .b(adder_13_cout), .out(adder_14_out), .cout(adder_14_cout));  // open: cin
  Subtractor #(.width(1)) subtractor_14 (
    .a(out13), .b(subtractor_13_bout), .out(subtractor_14_out), .bout(subtractor_14_bout));  // open: bin
  Multiplexer #(.select(2), .enable("false")) multiplexer_15 (
    .in0(not_2_out), .in1(i14), .in2(adder_15_out), .in3(subtractor_15_out), .out(multiplexer_15_out),
    .sel(FunSel));
  D_Flip_Flop d_ff_15 (.clk(CLK), .D(multiplexer_15_out), .Q(out14), .en(Enable));  // open: Qn, preset, reset
  Adder #(.width(1)) adder_15 (.a(out14), .b(adder_14_cout), .out(adder_15_out), .cout(adder_15_cout));  // open: cin
  Subtractor #(.width(1)) subtractor_15 (
    .a(out14), .b(subtractor_14_bout), .out(subtractor_15_out), .bout(subtractor_15_bout));  // open: bin
  Multiplexer #(.select(2), .enable("false")) multiplexer_16 (
    .in0(not_2_out), .in1(i15), .in2(adder_16_out), .in3(subtractor_16_out), .out(multiplexer_16_out),
    .sel(FunSel));
  D_Flip_Flop d_ff_16 (.clk(CLK), .D(multiplexer_16_out), .Q(out15), .en(Enable));  // open: Qn, preset, reset
  Adder #(.width(1)) adder_16 (.a(out15), .b(adder_15_cout), .out(adder_16_out));  // open: cin, cout
  Subtractor #(.width(1)) subtractor_16 (
    .a(out15), .b(subtractor_15_bout), .out(subtractor_16_out));  // open: bin, bout
endmodule
