// Logisim project proj2part1.circ as structural Verilog: 9 circuits, main circuit main
module ALU (
  input  [7:0] A,
  input  [7:0] B,
  input  Carry_In,
  input  [3:0] FunSel,
  output [7:0] OutALU,
  output [3:0] OutFlag
);

  wire adder_1_cout, adder_2_cout, and_1_out, and_2_out, and_3_out, and_4_out, CSL_carry_out, CSR_carry_out,
       LSL_carry_out, LSR_carry_out, not_1_out, not_2_out, not_3_out, not_4_out, not_5_out, or_1_out,
       or_2_out, subtractor_1_bout, xor_1_out;
  wire [7:0] A_and_B_out, A_or_B_out, A_xor_B_out, adder_1_out, adder_2_out, ASL_output, ASR_output,
       CSL_output, CSR_output, LSL_output, LSR_output, not_6_out, not_7_out, subtractor_1_out;

  Hex_Digit_Display hex_digit_display_1 (.value(A[7:4]));  // open: dp
  Hex_Digit_Display hex_digit_display_2 (.value(A[3:0]));  // open: dp
  assign A_and_B_out = A & B;  // AND_Gate A_and_B, 8 bits wide
  assign A_or_B_out = A | B;  // OR_Gate A_or_B, 8 bits wide
  LSL LSL (.Input(A), .Output(LSL_output), .Carry_Out(LSL_carry_out));
  nor nor_1 (OutFlag[3], OutALU[0], OutALU[1], OutALU[2], OutALU[3], OutALU[4], OutALU[5], OutALU[6], OutALU[7]);
  not not_1 (not_1_out, A[7]);
  not not_2 (not_2_out, B[7]);
  not not_3 (not_3_out, OutALU[7]);
  xor xor_1 (xor_1_out, A[7], OutALU[7]);
  not not_4 (not_4_out, Carry_In);
  Subtractor subtractor_1 (.a(A), .b(B), .out(subtractor_1_out), .bin(not_4_out), .bout(subtractor_1_bout));
  not not_5 (not_5_out, subtractor_1_bout);
  LSR LSR (.Input(A), .Carry_Out(LSR_carry_out), .Output(LSR_output));
  ASL ASL (.Input(A), .Output(ASL_output));
  and and_1 (and_1_out, not_1_out, not_2_out, OutALU[7]);
  and and_2 (and_2_out, B[7], A[7], not_3_out);
  and and_3 (and_3_out, B[7], not_1_out, OutALU[7]);
  and and_4 (and_4_out, not_3_out, A[7], not_2_out);
  Adder adder_1 (.a(A), .b(B), .out(adder_1_out), .cin(Carry_In), .cout(adder_1_cout));
  ASR ASR (.Input(A), .Output(ASR_output));
  CSL CSL (.Carry_In(Carry_In), .Input(A), .Output(CSL_output), .Carry_Out(CSL_carry_out));
  or or_1 (or_1_out, and_1_out, and_2_out);
  or or_2 (or_2_out, and_3_out, and_4_out);
  Hex_Digit_Display hex_digit_display_3 (.value(B[7:4]));  // open: dp
  Adder adder_2 (.a(A), .b(B), .out(adder_2_out), .cout(adder_2_cout));  // open: cin
  CSR CSR (.Input(A), .Carry_In(Carry_In), .Carry_Out(CSR_carry_out), .Output(CSR_output));
  Hex_Digit_Display hex_digit_display_4 (.value(B[3:0]));  // open: dp
  assign not_6_out = ~A;  // NOT_Gate not_6, 8 bits wide
  assign not_7_out = ~B;  // NOT_Gate not_7, 8 bits wide
  Multiplexer #(.select(4)) multiplexer_1 (
    .in0(1'b0), .in1(1'b0), .in2(1'b0), .in3(1'b0), .in4(or_1_out), .in5(or_1_out), .in6(or_2_out),
    .in7(1'b0), .in8(1'b0), .in9(1'b0), .in10(1'b0), .in11(1'b0), .in12(xor_1_out), .in13(1'b0),
    .in14(xor_1_out), .in15(xor_1_out), .out(OutFlag[0]), .sel(FunSel));  // open: en
  assign A_xor_B_out = A ^ B;  // XOR_Gate A_xor_B, 8 bits wide
  Multiplexer #(.select(4), .width(8)) multiplexer_2 (
    .in0(A), .in1(B), .in2(not_6_out), .in3(not_7_out), .in4(adder_2_out), .in5(adder_1_out),
    .in6(subtractor_1_out), .in7(A_and_B_out), .in8(A_or_B_out), .in9(A_xor_B_out), .in10(LSL_output),
    .in11(LSR_output), .in12(ASL_output), .in13(ASR_output), .in14(CSL_output), .in15(CSR_output),
    .out(OutALU), .sel(FunSel));  // open: en
  Multiplexer #(.select(4)) multiplexer_3 (
    .in0(Carry_In), .in1(Carry_In), .in2(Carry_In), .in3(Carry_In), .in4(adder_2_cout), .in5(adder_1_cout),
    .in6(not_5_out), .in7(Carry_In), .in8(Carry_In), .in9(Carry_In), .in10(LSL_carry_out),
    .in11(LSR_carry_out), .in12(Carry_In), .in13(Carry_In), .in14(CSL_carry_out), .in15(CSR_carry_out),
    .out(OutFlag[2]), .sel(FunSel));  // open: en
  Hex_Digit_Display hex_digit_display_5 (.value(OutALU[7:4]));  // open: dp
  Hex_Digit_Display hex_digit_display_6 (.value(OutALU[3:0]));  // open: dp

  assign OutFlag[1] = OutALU[7];

  // Notes on the sheet:
  //   A
  //   B
endmodule

module LSL (
  input  [7:0] Input,
  output [7:0] Output,
  output Carry_Out
);


  assign Carry_Out = Input[7];
  assign Output = {Input[6:0], 1'b0};
endmodule

module LSR (
  input  [7:0] Input,
  output Carry_Out,
  output [7:0] Output
);


  assign Carry_Out = Input[0];
  assign Output = {1'b0, Input[7:1]};
endmodule

module ASL (
  input  [7:0] Input,
  output [7:0] Output
);


  assign Output = {Input[6:0], 1'b0};
endmodule

module ASR (
  input  [7:0] Input,
  output [7:0] Output
);


  assign Output = {{2{Input[7]}}, Input[6:1]};
endmodule

module CSL (
  input  Carry_In,
  input  [7:0] Input,
  output [7:0] Output,
  output Carry_Out
);


  assign Carry_Out = Input[7];
  assign Output = {Input[6:0], Carry_In};
endmodule

module CSR (
  input  [7:0] Input,
  input  Carry_In,
  output Carry_Out,
  output [7:0] Output
);


  assign Carry_Out = Input[0];
  assign Output = {Carry_In, Input[7:1]};
endmodule

module FR (
  input  CLK,
  input  Input,
  output Output
);

  D_Flip_Flop d_ff_1 (.clk(CLK), .D(Input), .Q(Output));  // open: Qn, preset, en, reset
endmodule

module main (
  input  [7:0] A,
  input  [7:0] B,
  input  [3:0] FunSel_prime,
  output [7:0] OutALU,
  output Z,
  output C,
  output N,
  output O
);

  wire CLK_out;
  wire [3:0] alu_1_outflag;

  Hex_Digit_Display hex_digit_display_1 (.value(A[7:4]));  // open: dp
  Hex_Digit_Display hex_digit_display_2 (.value(A[3:0]));  // open: dp
  Hex_Digit_Display hex_digit_display_3 (.value(B[3:0]));  // open: dp
  Hex_Digit_Display hex_digit_display_4 (.value(B[7:4]));  // open: dp
  ALU alu_1 (.A(A), .B(B), .Carry_In(C), .FunSel(FunSel_prime), .OutALU(OutALU), .OutFlag(alu_1_outflag));
  Clock CLK (.out(CLK_out));
  FR u_Z (.CLK(CLK_out), .Input(alu_1_outflag[3]), .Output(Z));
  FR u_C (.CLK(CLK_out), .Input(alu_1_outflag[2]), .Output(C));
  Hex_Digit_Display hex_digit_display_5 (.value(OutALU[7:4]));  // open: dp
  Hex_Digit_Display hex_digit_display_6 (.value(OutALU[3:0]));  // open: dp
  FR u_N (.CLK(CLK_out), .Input(alu_1_outflag[1]), .Output(N));
  FR u_O (.CLK(CLK_out), .Input(alu_1_outflag[0]), .Output(O));

  // Notes on the sheet:
  //   A
  //   B
endmodule
