// Logisim project proj1part2a.circ as structural Verilog: 2 circuits, main circuit main
module main (
  input  [7:0] Input,
  input  [1:0] OutASel,
  input  [1:0] OutBSel,
  input  [3:0] RegSel,
  input  [1:0] FunSel,
  output [7:0] OutA,
  output [7:0] OutB
);

  wire CLK_out;

  Hex_Digit_Display hex_digit_display_1 (.value(Input[7:4]));  // open: dp
  Hex_Digit_Display hex_digit_display_2 (.value(Input[3:0]));  // open: dp
  Clock CLK (.out(CLK_out));
  _2a u_2a_1 (
    .Input(Input), .OutASel(OutASel), .OutBSel(OutBSel), .RegSel(RegSel), .FunSel(FunSel), .CLK(CLK_out),
    .OutA(OutA), .OutB(OutB));
  Hex_Digit_Display hex_digit_display_3 (.value(OutA[7:4]));  // open: dp
  Hex_Digit_Display hex_digit_display_4 (.value(OutA[3:0]));  // open: dp
  Hex_Digit_Display hex_digit_display_5 (.value(OutB[7:4]));  // open: dp
  Hex_Digit_Display hex_digit_display_6 (.value(OutB[3:0]));  // open: dp
endmodule

module _2a (
  input  [7:0] Input,
  input  [1:0] OutASel,
  input  [1:0] OutBSel,
  input  [3:0] RegSel,
  input  [1:0] FunSel,
  input  CLK,
  output [7:0] OutA,
  output [7:0] OutB
);

  wire [7:0] R0_output, R1_output, R2_output, R3_output;

  Hex_Digit_Display hex_digit_display_1 (.value(Input[3:0]));  // open: dp
  Hex_Digit_Display hex_digit_display_2 (.value(Input[7:4]));  // open: dp
  _8_bit R0 (.Input(Input), .FunSel(FunSel), .CLK(CLK), .Enable(RegSel[0]), .Output(R0_output));
  _8_bit R1 (.Input(Input), .FunSel(FunSel), .CLK(CLK), .Enable(RegSel[1]), .Output(R1_output));
  _8_bit R2 (.Input(Input), .FunSel(FunSel), .CLK(CLK), .Enable(RegSel[2]), .Output(R2_output));
  _8_bit R3 (.Input(Input), .FunSel(FunSel), .CLK(CLK), .Enable(RegSel[3]), .Output(R3_output));
  Multiplexer #(.select(2), .width(8), .enable("false")) multiplexer_1 (
    .in0(R0_output), .in1(R1_output), .in2(R2_output), .in3(R3_output), .out(OutA), .sel(OutASel));
  Multiplexer #(.select(2), .width(8), .enable("false")) multiplexer_2 (
    .in0(R0_output), .in1(R1_output), .in2(R2_output), .in3(R3_output), .out(OutB), .sel(OutBSel));
  Hex_Digit_Display hex_digit_display_3 (.value(OutA[7:4]));  // open: dp
  Hex_Digit_Display hex_digit_display_4 (.value(OutA[3:0]));  // open: dp
  Hex_Digit_Display hex_digit_display_5 (.value(OutB[7:4]));  // open: dp
  Hex_Digit_Display hex_digit_display_6 (.value(OutB[3:0]));  // open: dp
endmodule
