// Logisim project proj3.circ as structural Verilog: 3 circuits, main circuit main
// 2
module main (
  output [1:0] OutCSel,
  output [1:0] OutASel,
  output [1:0] OutBSel,
  output [1:0] OutDSel,
  output [2:0] RegSelARF,
  output [1:0] MuxASel,
  output [3:0] RegSelRF,
  output [3:0] FunSelALU,
  output MuxCSel,
  output [1:0] FunSelRF,
  output [1:0] FunSelARF,
  output SC_Clear,
  output [1:0] MuxBSel
);

  wire and_1_out, and_2_out, and_3_out, and_4_out, and_5_out, and_6_out, and_7_out, and_8_out, and_9_out,
       and_10_out, and_11_out, and_12_out, and_13_out, and_14_out, and_15_out, and_16_out, and_17_out,
       and_18_out, and_19_out, and_20_out, and_21_out, and_22_out, and_23_out, and_24_out, and_25_out,
       and_26_out, and_27_out, and_28_out, and_29_out, and_30_out, and_31_out, and_32_out, and_33_out,
       and_34_out, and_35_out, and_36_out, and_37_out, and_38_out, and_39_out, and_40_out, and_41_out,
       and_42_out, and_43_out, and_44_out, and_45_out, and_46_out, and_47_out, and_48_out, and_49_out,
       and_50_out, and_51_out, and_52_out, and_53_out, and_54_out, and_55_out, and_56_out, and_57_out,
       and_58_out, and_59_out, and_60_out, and_61_out, and_62_out, and_63_out, and_64_out, and_65_out,
       and_66_out, and_67_out, and_68_out, and_69_out, and_70_out, and_71_out, and_72_out, and_73_out,
       and_74_out, and_75_out, and_76_out, and_77_out, and_78_out, and_79_out, and_80_out, and_81_out,
       and_82_out, and_83_out, and_84_out, and_85_out, and_86_out, and_87_out, and_88_out, and_89_out,
       and_90_out, and_91_out, and_92_out, and_93_out, and_94_out, and_95_out, and_96_out, and_97_out,
       and_98_out, and_99_out, and_100_out, and_101_out, and_102_out, and_103_out, and_104_out, and_105_out,
       and_106_out, and_107_out, and_108_out, and_109_out, and_110_out, and_111_out, and_112_out,
       and_113_out, and_114_out, and_115_out, and_116_out, and_117_out, and_118_out, and_119_out,
       and_120_out, and_121_out, and_122_out, and_123_out, and_124_out, and_125_out, and_126_out,
       and_127_out, and_128_out, and_129_out, and_130_out, and_131_out, and_132_out, and_133_out,
       and_134_out, and_135_out, and_136_out, and_137_out, and_138_out, and_139_out, and_140_out,
       and_141_out, and_142_out, and_143_out, and_144_out, and_145_out, and_146_out, and_147_out,
       and_148_out, and_149_out, and_150_out, and_151_out, and_152_out, and_153_out, and_154_out,
       and_155_out, and_156_out, and_157_out, and_158_out, and_159_out, and_160_out, and_161_out,
       and_162_out, and_163_out, and_164_out, and_165_out, and_166_out, and_167_out, and_168_out,
       and_169_out, and_170_out, and_171_out, and_172_out, and_173_out, and_174_out, and_175_out,
       and_176_out, and_177_out, and_178_out, and_179_out, and_180_out, and_181_out, and_182_out,
       and_183_out, and_184_out, and_185_out, and_186_out, CLK_out, D0, D0_D4, D1, D1_D3_D4_D18, D2,
       D2_D5_D9_D10_D11_D12_D13_D14_D15_D16, D2_D11_D12_D13, D2_D12_D13, D3, D4, D5, D5_D6_D9_D10, D5_D9_D10,
       D6, D7, D7_D8, D8, D9, D9_D10, D10, D11, D11_D12_D13, D12, D13, D14, D15, D16, D17, D18, d_ff_1_q, En,
       IR0, IR1, IR2, IR3, IR4, IR5, IR6, IR7, IR8, IR9, IR10, IR11, IR12, IR13, IR14, IR15, L_H, Load,
       nor_1_out, not_1_out, not_2_out, not_3_out, not_4_out, not_5_out, not_6_out, not_7_out, not_8_out,
       not_9_out, not_10_out, not_11_out, not_12_out, not_13_out, not_14_out, not_15_out, not_16_out,
       not_17_out, not_18_out, not_19_out, not_20_out, not_21_out, not_22_out, not_23_out, not_24_out,
       not_25_out, not_26_out, not_27_out, not_28_out, not_29_out, not_30_out, not_31_out, not_32_out,
       not_33_out, not_34_out, not_35_out, not_36_out, not_37_out, not_38_out, not_39_out, not_40_out,
       not_41_out, not_42_out, not_43_out, not_44_out, not_45_out, not_46_out, not_47_out, not_48_out,
       not_49_out, not_50_out, not_51_out, not_52_out, not_53_out, not_54_out, not_55_out, not_56_out,
       not_57_out, not_58_out, not_59_out, not_60_out, not_61_out, not_62_out, not_63_out, not_64_out,
       not_65_out, not_66_out, not_67_out, not_68_out, not_69_out, not_70_out, not_71_out, not_72_out,
       not_73_out, not_74_out, not_75_out, not_76_out, not_77_out, not_78_out, not_79_out, not_80_out,
       not_81_out, not_82_out, not_83_out, not_84_out, not_85_out, not_86_out, not_87_out, not_88_out,
       not_89_out, not_90_out, not_91_out, not_92_out, not_93_out, not_94_out, not_95_out, not_96_out,
       not_97_out, not_98_out, not_99_out, not_100_out, not_101_out, not_102_out, not_103_out, not_104_out,
       not_105_out, not_106_out, not_107_out, not_108_out, not_109_out, not_110_out, not_111_out,
       not_112_out, not_113_out, not_114_out, not_115_out, not_116_out, not_117_out, not_118_out,
       not_119_out, not_120_out, not_121_out, not_122_out, not_123_out, not_124_out, not_125_out,
       not_126_out, not_127_out, not_128_out, not_129_out, not_130_out, not_131_out, not_132_out,
       not_133_out, not_134_out, not_135_out, not_136_out, not_137_out, not_138_out, not_139_out,
       not_140_out, not_141_out, not_142_out, not_143_out, not_144_out, not_145_out, not_146_out,
       not_147_out, not_148_out, not_149_out, not_150_out, not_151_out, not_152_out, not_153_out,
       not_154_out, not_155_out, not_156_out, not_157_out, not_158_out, not_159_out, not_160_out,
       not_161_out, not_162_out, not_163_out, not_164_out, not_165_out, not_166_out, not_167_out,
       not_168_out, not_169_out, not_170_out, not_171_out, not_172_out, not_173_out, not_174_out,
       not_175_out, not_176_out, not_177_out, not_178_out, not_179_out, not_180_out, not_181_out,
       not_182_out, not_183_out, not_184_out, not_185_out, not_186_out, not_187_out, not_188_out,
       not_189_out, not_190_out, not_191_out, not_192_out, not_193_out, not_194_out, not_195_out,
       not_196_out, not_197_out, not_198_out, not_199_out, not_200_out, not_201_out, not_202_out,
       not_203_out, not_204_out, not_205_out, not_206_out, not_207_out, not_208_out, or_1_out, or_2_out,
       or_3_out, or_4_out, or_5_out, or_6_out, or_7_out, or_8_out, or_9_out, or_10_out, or_11_out, or_12_out,
       or_13_out, or_14_out, or_15_out, or_16_out, or_17_out, or_18_out, or_19_out, or_20_out, or_21_out,
       or_22_out, or_23_out, or_24_out, or_25_out, or_26_out, or_27_out, or_28_out, or_29_out, or_30_out,
       or_31_out, or_32_out, or_33_out, or_34_out, or_35_out, or_36_out, or_37_out, or_38_out, or_39_out,
       or_40_out, or_41_out, or_42_out, or_43_out, or_44_out, or_45_out, SRC__DEST, Store, T0, T1, T2, T3,
       T4, T5, T6, xnor_1_out, xnor_2_out, Z;
  wire [1:0] FunSelIR;
  wire [2:0] arfdecoder_1_output, arfdecoder_2_output, counter_1_q;
  wire [3:0] rfdecoder_1_output, rfdecoder_2_output, rfdecoder_3_output;

  and and_1 (and_1_out, D0, T5);
  and and_2 (and_2_out, D1, T5);
  and and_3 (and_3_out, D3, T4);
  and and_4 (and_4_out, D4, T5);
  and and_5 (and_5_out, D17, T4);
  and and_6 (and_6_out, D18, T5);
  or or_1 (or_1_out, T0, T1, T2, T3);
  or or_2 (or_2_out, and_1_out, and_2_out);
  or or_3 (or_3_out, and_3_out, and_4_out, and_5_out, and_6_out);
  assign OutDSel = or_1_out ? 2'b00 : 2'bz;  // Controlled_Buffer controlled_buffer_1
  assign OutDSel = or_2_out ? 2'b01 : 2'bz;  // Controlled_Buffer controlled_buffer_2
  assign OutDSel = or_3_out ? 2'b10 : 2'bz;  // Controlled_Buffer controlled_buffer_3
  not not_1 (not_1_out, IR4);
  not not_2 (not_2_out, IR7);
  not not_3 (not_3_out, IR4);
  not not_4 (not_4_out, IR7);
  not not_5 (not_5_out, IR10);
  not not_6 (not_6_out, IR4);
  not not_7 (not_7_out, IR7);
  and and_7 (and_7_out, D1, T5);
  and and_8 (and_8_out, D3, T4);
  and and_9 (and_9_out, D2_D12_D13, T4, not_8_out, not_9_out);
  not not_8 (not_8_out, IR7);
  not not_9 (not_9_out, IR10);
  and and_10 (and_10_out, D2_D12_D13, T4, not_10_out, IR10);
  not not_10 (not_10_out, IR7);
  and and_11 (and_11_out, D5_D9_D10, T4, not_11_out, not_12_out, not_13_out);
  not not_11 (not_11_out, IR4);
  not not_12 (not_12_out, IR7);
  not not_13 (not_13_out, IR10);
  and and_12 (and_12_out, D5_D9_D10, T4, not_1_out, not_2_out, IR10);
  and and_13 (and_13_out, D6, T4, not_3_out, not_4_out, not_5_out);
  and and_14 (and_14_out, D6, T4, not_6_out, not_7_out, IR10);
  or or_4 (or_4_out, and_7_out, and_8_out);
  or or_5 (or_5_out, and_9_out, and_10_out, and_11_out, and_12_out);
  or or_6 (or_6_out, and_13_out, and_14_out);
  assign OutASel = or_4_out ? {IR10, IR9} : 2'bz;  // Controlled_Buffer controlled_buffer_4
  assign OutASel = or_5_out ? {IR6, IR5} : 2'bz;  // Controlled_Buffer controlled_buffer_5
  assign OutASel = or_6_out ? {IR3, IR2} : 2'bz;  // Controlled_Buffer controlled_buffer_6
  not not_14 (not_14_out, IR4);
  not not_15 (not_15_out, IR7);
  not not_16 (not_16_out, IR10);
  not not_17 (not_17_out, IR4);
  not not_18 (not_18_out, IR7);
  not not_19 (not_19_out, IR4);
  not not_20 (not_20_out, IR7);
  not not_21 (not_21_out, IR4);
  not not_22 (not_22_out, IR7);
  not not_23 (not_23_out, IR7);
  not not_24 (not_24_out, IR10);
  not not_25 (not_25_out, IR4);
  not not_26 (not_26_out, IR4);
  not not_27 (not_27_out, IR7);
  not not_28 (not_28_out, IR10);
  not not_29 (not_29_out, IR7);
  not not_30 (not_30_out, IR10);
  not not_31 (not_31_out, IR4);
  not not_32 (not_32_out, IR7);
  not not_33 (not_33_out, IR7);
  and and_15 (and_15_out, D5_D9_D10, T4, not_14_out, not_15_out, not_16_out);
  and and_16 (and_16_out, D5_D9_D10, T4, not_17_out, not_18_out, IR10);
  and and_17 (and_17_out, D5, T4, not_19_out, IR7, IR10);
  and and_18 (and_18_out, D5_D9_D10, T4, IR4, not_20_out, IR10);
  and and_19 (and_19_out, D10, T4, not_21_out, not_22_out, IR10);
  and and_20 (and_20_out, D11, T4, not_23_out, not_24_out);
  and and_21 (and_21_out, D9, T4, not_25_out, IR7, IR10);
  and and_22 (and_22_out, D6, T4, not_26_out, not_27_out, not_28_out);
  and and_23 (and_23_out, D6, T4, IR4, not_29_out, not_30_out);
  and and_24 (and_24_out, D6, T4, not_31_out, not_32_out, IR10);
  and and_25 (and_25_out, D6, T4, IR4, not_33_out, IR10);
  or or_7 (or_7_out, and_15_out, and_16_out, and_17_out);
  assign OutBSel = or_7_out ? {IR3, IR2} : 2'bz;  // Controlled_Buffer controlled_buffer_7
  or or_8 (or_8_out, and_18_out, and_19_out, and_20_out, and_21_out, and_22_out, and_23_out, and_24_out, and_25_out);
  assign OutBSel = or_8_out ? {IR6, IR5} : 2'bz;  // Controlled_Buffer controlled_buffer_8
  not not_34 (not_34_out, IR10);
  not not_35 (not_35_out, IR4);
  not not_36 (not_36_out, IR10);
  not not_37 (not_37_out, SRC__DEST);
  not not_38 (not_38_out, IR7);
  not not_39 (not_39_out, SRC__DEST);
  and and_26 (and_26_out, D5_D9_D10, T4, IR4, not_40_out, IR10);
  not not_40 (not_40_out, IR7);
  and and_27 (and_27_out, D6, T4, IR4, not_41_out, not_42_out);
  not not_41 (not_41_out, IR7);
  not not_42 (not_42_out, IR10);
  and and_28 (and_28_out, D6, T4, IR4, not_43_out, IR10);
  not not_43 (not_43_out, IR7);
  and and_29 (and_29_out, D9_D10, T4, not_44_out, not_45_out, not_46_out);
  not not_44 (not_44_out, IR4);
  not not_45 (not_45_out, IR7);
  not not_46 (not_46_out, IR10);
  and and_30 (and_30_out, D2, T4, IR7, not_34_out);
  and and_31 (and_31_out, D2, T4, IR7, IR10);
  and and_32 (and_32_out, D5, T4, not_35_out, IR7, IR10);
  and and_33 (and_33_out, D11_D12_D13, T4, IR4, IR7, IR10);
  and and_34 (and_34_out, D7_D8, T5, IR7, not_36_out);
  and and_35 (and_35_out, D7_D8, T4, SRC__DEST, IR7, IR10);
  and and_36 (and_36_out, D7_D8, T5, not_37_out, IR7, IR10);
  and and_37 (and_37_out, D17, T4);
  and and_38 (and_38_out, D7_D8, T6, not_38_out, IR10);
  and and_39 (and_39_out, D7_D8, T6, not_39_out, IR7, IR10);
  or or_9 (or_9_out, and_26_out, and_27_out, and_28_out, and_29_out);
  or or_10 (or_10_out, and_34_out, and_30_out, and_31_out, and_35_out, and_32_out, and_33_out, and_36_out);
  or or_11 (or_11_out, and_38_out, and_39_out);
  assign OutCSel = or_9_out ? {IR3, IR2} : 2'bz;  // Controlled_Buffer controlled_buffer_9
  assign OutCSel = or_10_out ? {IR6, IR5} : 2'bz;  // Controlled_Buffer controlled_buffer_10
  assign OutCSel = and_37_out ? 2'b00 : 2'bz;  // Controlled_Buffer controlled_buffer_11
  assign OutCSel = or_11_out ? {IR9, IR8} : 2'bz;  // Controlled_Buffer controlled_buffer_12
  not not_47 (not_47_out, IR10);
  not not_48 (not_48_out, IR7);
  not not_49 (not_49_out, IR10);
  not not_50 (not_50_out, IR7);
  not not_51 (not_51_out, IR4);
  not not_52 (not_52_out, IR8);
  not not_53 (not_53_out, IR10);
  not not_54 (not_54_out, IR10);
  not not_55 (not_55_out, IR7);
  not not_56 (not_56_out, IR10);
  not not_57 (not_57_out, IR7);
  not not_58 (not_58_out, SRC__DEST);
  not not_59 (not_59_out, IR10);
  not not_60 (not_60_out, IR10);
  not not_61 (not_61_out, IR7);
  not not_62 (not_62_out, IR7);
  not not_63 (not_63_out, IR10);
  not not_64 (not_64_out, IR7);
  not not_65 (not_65_out, SRC__DEST);
  not not_66 (not_66_out, IR7);
  not not_67 (not_67_out, IR10);
  not not_68 (not_68_out, IR7);
  not not_69 (not_69_out, SRC__DEST);
  not not_70 (not_70_out, IR7);
  not not_71 (not_71_out, IR10);
  not not_72 (not_72_out, IR7);
  not not_73 (not_73_out, IR7);
  not not_74 (not_74_out, Z);
  and and_40 (and_40_out, D7_D8, T5, not_56_out, not_57_out, not_58_out);
  and and_41 (and_41_out, D7_D8, T5, not_59_out, IR7);
  and and_42 (and_42_out, D7, T4, not_60_out, not_61_out);
  and and_43 (and_43_out, D7, T4, IR10, not_62_out);
  and and_44 (and_44_out, D8, T6, not_63_out, not_64_out, not_65_out);
  and and_45 (and_45_out, D8, T6, IR10, not_66_out);
  and and_46 (and_46_out, D7, T6, not_67_out, not_68_out, not_69_out);
  and and_47 (and_47_out, D7, T6, IR10, not_70_out);
  and and_48 (and_48_out, D8, T4, not_71_out, not_72_out);
  and and_49 (and_49_out, D8, T4, IR10, not_73_out);
  and and_50 (and_50_out, D1, T4);
  and and_51 (and_51_out, D0, T4, IR8);
  and and_52 (and_52_out, D14, T4);
  and and_53 (and_53_out, D15, T4, Z);
  and and_54 (and_54_out, D16, T4, not_74_out);
  and and_55 (and_55_out, D17, T6);
  and and_56 (and_56_out, D2_D11_D12_D13, T4, not_47_out, not_48_out);
  and and_57 (and_57_out, D5_D6_D9_D10, T4, not_49_out, not_50_out, not_51_out);
  and and_58 (and_58_out, D0_D4, T5);
  and and_59 (and_59_out, D0, not_52_out, T4);
  and and_60 (and_60_out, D2, T4, IR7, not_53_out);
  and and_61 (and_61_out, D6, T5, not_54_out, not_55_out, IR4);
  or or_12 (or_12_out, and_50_out, and_51_out, and_52_out, and_53_out, and_54_out, and_55_out);
  assign MuxBSel = or_12_out ? 2'b01 : 2'bz;  // Controlled_Buffer controlled_buffer_13
  nor nor_1 (nor_1_out, or_12_out, and_62_out);
  and and_62 (and_62_out, D18, T5);
  assign MuxBSel = and_62_out ? 2'b10 : 2'bz;  // Controlled_Buffer controlled_buffer_14
  or or_13 (or_13_out, and_40_out, and_56_out, and_57_out, and_58_out, and_59_out, and_60_out, and_61_out, and_41_out);
  or or_14 (or_14_out, and_42_out, and_43_out, and_44_out, and_45_out);
  assign FunSelRF = or_14_out ? 2'b11 : 2'bz;  // Controlled_Buffer controlled_buffer_15
  or or_15 (or_15_out, and_46_out, and_47_out, and_48_out, and_49_out);
  assign FunSelRF = or_15_out ? 2'b10 : 2'bz;  // Controlled_Buffer controlled_buffer_16
  assign MuxBSel = nor_1_out ? 2'b11 : 2'bz;  // Controlled_Buffer controlled_buffer_17
  assign FunSelRF = or_13_out ? 2'b01 : 2'bz;  // Controlled_Buffer controlled_buffer_18
  not not_75 (not_75_out, IR10);
  and and_63 (and_63_out, D4, T4);
  not not_76 (not_76_out, IR10);
  and and_64 (and_64_out, not_76_out, IR7, D7, T6);
  and and_65 (and_65_out, IR10, IR7, SRC__DEST, D7, T6);
  not not_77 (not_77_out, IR10);
  and and_66 (and_66_out, not_77_out, IR7, D7, T4);
  not not_78 (not_78_out, IR10);
  and and_67 (and_67_out, not_78_out, IR7, D7, T4);
  not not_79 (not_79_out, IR10);
  and and_68 (and_68_out, not_79_out, IR7, D8, T6);
  and and_69 (and_69_out, D3, T5);
  and and_70 (and_70_out, IR10, IR7, SRC__DEST, D8, T6);
  and and_71 (and_71_out, not_75_out, IR7, D7, T4);
  not not_80 (not_80_out, IR10);
  and and_72 (and_72_out, not_80_out, IR7, D7, T4);
  not not_81 (not_81_out, IR10);
  not not_82 (not_82_out, IR7);
  not not_83 (not_83_out, IR4);
  not not_84 (not_84_out, IR7);
  not not_85 (not_85_out, IR4);
  not not_86 (not_86_out, IR7);
  not not_87 (not_87_out, IR10);
  not not_88 (not_88_out, IR7);
  or or_16 (or_16_out, T1, T3, and_63_out, and_64_out, and_65_out, and_66_out, and_67_out);
  or or_17 (or_17_out, and_72_out, and_68_out, and_69_out, and_71_out, and_70_out);
  and and_73 (and_73_out, D5_D6_D9_D10, T4, not_81_out, not_82_out, not_83_out);
  and and_74 (and_74_out, D5_D6_D9_D10, T4, IR10, not_84_out, not_85_out);
  and and_75 (and_75_out, D1, T5);
  and and_76 (and_76_out, D3, T4);
  and and_77 (and_77_out, D2, T4, IR10, not_86_out);
  and and_78 (and_78_out, D12, T4, not_87_out, not_88_out);
  assign FunSelARF = or_16_out ? 2'b10 : 2'bz;  // Controlled_Buffer controlled_buffer_19
  assign FunSelARF = or_17_out ? 2'b11 : 2'bz;  // Controlled_Buffer controlled_buffer_20
  or or_18 (or_18_out, or_16_out, or_17_out);
  not not_89 (not_89_out, or_18_out);
  assign FunSelARF = not_89_out ? 2'b01 : 2'bz;  // Controlled_Buffer controlled_buffer_21
  not not_90 (not_90_out, or_19_out);
  or or_19 (or_19_out, and_73_out, and_74_out, and_75_out, and_76_out, and_77_out, and_78_out);
  assign MuxCSel = not_90_out ? 1'b0 : 1'bz;  // Controlled_Buffer controlled_buffer_22
  assign MuxCSel = or_19_out ? 1'b1 : 1'bz;  // Controlled_Buffer controlled_buffer_23
  not not_91 (not_91_out, IR8);
  not not_92 (not_92_out, IR10);
  not not_93 (not_93_out, IR7);
  not not_94 (not_94_out, IR10);
  not not_95 (not_95_out, IR10);
  not not_96 (not_96_out, IR7);
  not not_97 (not_97_out, IR4);
  not not_98 (not_98_out, IR10);
  not not_99 (not_99_out, IR7);
  not not_100 (not_100_out, IR10);
  not not_101 (not_101_out, IR7);
  not not_102 (not_102_out, SRC__DEST);
  not not_103 (not_103_out, IR10);
  not not_104 (not_104_out, IR10);
  not not_105 (not_105_out, IR7);
  not not_106 (not_106_out, IR10);
  not not_107 (not_107_out, IR7);
  not not_108 (not_108_out, SRC__DEST);
  not not_109 (not_109_out, IR7);
  not not_110 (not_110_out, IR7);
  and and_79 (and_79_out, D0, T4, not_91_out);
  and and_80 (and_80_out, D0, T5, IR8);
  and and_81 (and_81_out, D4, T5);
  and and_82 (and_82_out, D2_D11_D12_D13, T4, not_92_out, not_93_out);
  and and_83 (and_83_out, D2, T4, not_94_out, IR7);
  and and_84 (and_84_out, D5_D6_D9_D10, T4, not_95_out, not_96_out, not_97_out);
  and and_85 (and_85_out, D6, T5, not_98_out, not_99_out, IR4);
  and and_86 (and_86_out, D7_D8, T5, not_100_out, not_101_out, not_102_out);
  and and_87 (and_87_out, D7_D8, T5, not_103_out, IR7);
  and and_88 (and_88_out, D7_D8, T4, not_104_out, not_105_out);
  and and_89 (and_89_out, D7_D8, T6, not_106_out, not_107_out, not_108_out);
  and and_90 (and_90_out, D7_D8, T4, IR10, not_109_out);
  and and_91 (and_91_out, D7_D8, T6, IR10, not_110_out);
  RFDecoder rfdecoder_1 (.Input({IR10, IR9}), .Output(rfdecoder_1_output));
  or or_20 (or_20_out, and_79_out, and_80_out, and_81_out);
  RFDecoder rfdecoder_2 (.Input({IR9, IR8}), .Output(rfdecoder_2_output));
  or or_21 (or_21_out, and_82_out, and_83_out, and_84_out, and_85_out, and_86_out, and_87_out);
  RFDecoder rfdecoder_3 (.Input({IR6, IR5}), .Output(rfdecoder_3_output));
  or or_22 (or_22_out, and_88_out, and_89_out, and_90_out, and_91_out);
  or or_23 (or_23_out, or_20_out, or_21_out, or_22_out);
  not not_111 (not_111_out, or_23_out);
  assign RegSelRF = not_111_out ? 4'b0000 : 4'bz;  // Controlled_Buffer controlled_buffer_24
  assign RegSelRF = or_20_out ? rfdecoder_1_output : 4'bz;  // Controlled_Buffer controlled_buffer_25
  assign RegSelRF = or_21_out ? rfdecoder_2_output : 4'bz;  // Controlled_Buffer controlled_buffer_26
  assign RegSelRF = or_22_out ? rfdecoder_3_output : 4'bz;  // Controlled_Buffer controlled_buffer_27
  not not_112 (not_112_out, SRC__DEST);
  not not_113 (not_113_out, IR10);
  not not_114 (not_114_out, IR10);
  not not_115 (not_115_out, IR7);
  not not_116 (not_116_out, IR4);
  not not_117 (not_117_out, IR7);
  not not_118 (not_118_out, IR7);
  not not_119 (not_119_out, IR4);
  not not_120 (not_120_out, IR7);
  not not_121 (not_121_out, IR7);
  not not_122 (not_122_out, SRC__DEST);
  and and_92 (and_92_out, D7_D8, T5, not_122_out, IR7, IR10);
  and and_93 (and_93_out, D7_D8, T6, not_112_out, IR7, IR10);
  and and_94 (and_94_out, D7_D8, T4, IR7, not_113_out);
  and and_95 (and_95_out, D7_D8, T6, IR7, not_114_out);
  and and_96 (and_96_out, D7_D8, T4, IR7, IR10);
  and and_97 (and_97_out, D14, T4);
  and and_98 (and_98_out, Z, D15, T4);
  not not_123 (not_123_out, Z);
  and and_99 (and_99_out, not_123_out, D16, T4);
  and and_100 (and_100_out, D17, T6);
  and and_101 (and_101_out, D18, T5);
  and and_102 (and_102_out, D0, T4, IR8);
  and and_103 (and_103_out, D1, T4);
  and and_104 (and_104_out, D3, T5);
  and and_105 (and_105_out, D4, T4);
  and and_106 (and_106_out, D17, T5);
  and and_107 (and_107_out, D18, T4);
  and and_108 (and_108_out, D2_D11_D12_D13, T4, not_115_out, IR10);
  and and_109 (and_109_out, D2_D11_D12_D13, T4, IR7, IR10);
  and and_110 (and_110_out, D5_D6_D9_D10, T4, not_116_out, not_117_out, IR10);
  and and_111 (and_111_out, D5_D6_D9_D10, T4, IR4, not_118_out, IR10);
  and and_112 (and_112_out, D5_D9_D10, T4, not_119_out, not_120_out, IR10);
  and and_113 (and_113_out, D7_D8, T5, not_121_out, IR10);
  or or_24 (or_24_out, T1, T3, and_97_out, and_98_out, and_99_out, and_100_out, and_101_out);
  or or_25 (or_25_out, and_102_out, and_103_out);
  or or_26 (or_26_out, and_104_out, and_105_out, and_106_out, and_107_out);
  ARFDecoder arfdecoder_1 (.Input({IR9, IR8}), .Output(arfdecoder_1_output));
  or or_27 (or_27_out, and_108_out, and_109_out, and_110_out, and_111_out, and_112_out, and_113_out, and_92_out);
  ARFDecoder arfdecoder_2 (.Input({IR6, IR5}), .Output(arfdecoder_2_output));
  or or_28 (or_28_out, and_93_out, and_94_out, and_95_out, and_96_out);
  assign RegSelARF = or_27_out ? arfdecoder_1_output : 3'bz;  // Controlled_Buffer controlled_buffer_28
  assign RegSelARF = or_28_out ? arfdecoder_2_output : 3'bz;  // Controlled_Buffer controlled_buffer_29
  or or_29 (or_29_out, or_24_out, or_25_out, or_28_out, or_26_out, or_27_out);
  not not_124 (not_124_out, or_29_out);
  assign RegSelARF = not_124_out ? 3'b000 : 3'bz;  // Controlled_Buffer controlled_buffer_30
  assign RegSelARF = or_24_out ? 3'b001 : 3'bz;  // Controlled_Buffer controlled_buffer_31
  assign RegSelARF = or_25_out ? 3'b010 : 3'bz;  // Controlled_Buffer controlled_buffer_32
  assign RegSelARF = or_26_out ? 3'b100 : 3'bz;  // Controlled_Buffer controlled_buffer_33
  not not_125 (not_125_out, IR10);
  not not_126 (not_126_out, IR7);
  not not_127 (not_127_out, IR4);
  not not_128 (not_128_out, IR7);
  not not_129 (not_129_out, IR10);
  not not_130 (not_130_out, IR10);
  not not_131 (not_131_out, IR7);
  not not_132 (not_132_out, SRC__DEST);
  not not_133 (not_133_out, IR10);
  not not_134 (not_134_out, IR7);
  not not_135 (not_135_out, IR10);
  not not_136 (not_136_out, IR7);
  not not_137 (not_137_out, IR4);
  not not_138 (not_138_out, IR10);
  not not_139 (not_139_out, IR7);
  not not_140 (not_140_out, IR10);
  not not_141 (not_141_out, IR7);
  not not_142 (not_142_out, SRC__DEST);
  not not_143 (not_143_out, IR8);
  and and_114 (and_114_out, D2, T4, IR7, not_125_out);
  and and_115 (and_115_out, D2_D11_D12_D13, T4, IR10, IR7);
  and and_116 (and_116_out, D5_D6_D9_D10, IR10, not_126_out, IR4, T4);
  and and_117 (and_117_out, D5_D9_D10, T4, IR10, IR7, not_127_out);
  and and_118 (and_118_out, D6, T4, not_128_out, IR4, not_129_out);
  and and_119 (and_119_out, D17, T4);
  and and_120 (and_120_out, D7_D8, T5, IR7, not_130_out);
  and and_121 (and_121_out, D7_D8, T6, not_131_out, IR10);
  and and_122 (and_122_out, D7_D8, T6, not_132_out, IR7, IR10);
  and and_123 (and_123_out, D7_D8, T6, IR7, IR10);
  and and_124 (and_124_out, D2_D11_D12_D13, T4, not_133_out, not_134_out);
  and and_125 (and_125_out, D5_D6_D9_D10, T4, not_135_out, not_136_out, not_137_out);
  and and_126 (and_126_out, D6, T5, IR4, not_138_out, not_139_out);
  and and_127 (and_127_out, D7_D8, T5, not_142_out, not_140_out, not_141_out);
  and and_128 (and_128_out, D0, IR8, T5);
  and and_129 (and_129_out, D4, T5);
  or or_30 (or_30_out, and_124_out, and_124_out, and_126_out, and_127_out);
  or or_31 (or_31_out, and_114_out, and_115_out, and_116_out, and_117_out, and_118_out, and_119_out, and_120_out, and_121_out, and_122_out, and_123_out);
  assign MuxASel = or_31_out ? 2'b10 : 2'bz;  // Controlled_Buffer controlled_buffer_34
  assign MuxASel = or_30_out ? 2'b11 : 2'bz;  // Controlled_Buffer controlled_buffer_35
  or or_32 (or_32_out, and_128_out, and_129_out);
  assign MuxASel = or_32_out ? 2'b01 : 2'bz;  // Controlled_Buffer controlled_buffer_36
  and and_130 (and_130_out, D0, T4, not_143_out);
  assign MuxASel = and_130_out ? 2'b00 : 2'bz;  // Controlled_Buffer controlled_buffer_37
  not not_144 (not_144_out, IR7);
  not not_145 (not_145_out, IR10);
  not not_146 (not_146_out, IR7);
  not not_147 (not_147_out, IR4);
  not not_148 (not_148_out, IR7);
  not not_149 (not_149_out, IR10);
  not not_150 (not_150_out, IR4);
  not not_151 (not_151_out, IR7);
  not not_152 (not_152_out, IR7);
  not not_153 (not_153_out, IR4);
  not not_154 (not_154_out, IR4);
  not not_155 (not_155_out, IR7);
  not not_156 (not_156_out, IR10);
  not not_157 (not_157_out, IR7);
  not not_158 (not_158_out, IR10);
  not not_159 (not_159_out, IR4);
  not not_160 (not_160_out, IR7);
  not not_161 (not_161_out, IR7);
  not not_162 (not_162_out, IR4);
  not not_163 (not_163_out, IR7);
  not not_164 (not_164_out, IR10);
  not not_165 (not_165_out, IR4);
  not not_166 (not_166_out, IR4);
  not not_167 (not_167_out, IR7);
  not not_168 (not_168_out, IR7);
  not not_169 (not_169_out, IR4);
  not not_170 (not_170_out, IR7);
  not not_171 (not_171_out, IR10);
  not not_172 (not_172_out, IR4);
  not not_173 (not_173_out, IR4);
  not not_174 (not_174_out, IR7);
  not not_175 (not_175_out, IR7);
  not not_176 (not_176_out, IR7);
  not not_177 (not_177_out, IR10);
  not not_178 (not_178_out, IR7);
  not not_179 (not_179_out, IR7);
  not not_180 (not_180_out, IR10);
  not not_181 (not_181_out, IR7);
  not not_182 (not_182_out, IR7);
  not not_183 (not_183_out, IR10);
  not not_184 (not_184_out, IR7);
  and and_131 (and_131_out, D1, T5);
  and and_132 (and_132_out, D2, T4, not_144_out, not_145_out);
  and and_133 (and_133_out, D2, T4, not_146_out, IR10);
  and and_134 (and_134_out, D2, T4, IR7, IR10);
  and and_135 (and_135_out, D3, T4);
  and and_136 (and_136_out, D17, T4);
  and and_137 (and_137_out, D5, T4, not_147_out, not_148_out, not_149_out);
  and and_138 (and_138_out, D5, T4, not_150_out, not_151_out, IR10);
  and and_139 (and_139_out, D5, T4, IR4, not_152_out, IR10);
  and and_140 (and_140_out, D5, T4, not_153_out, IR7, IR10);
  and and_141 (and_141_out, D6, T4, not_154_out, not_155_out, not_156_out);
  and and_142 (and_142_out, D6, T5, IR4, not_157_out, not_158_out);
  and and_143 (and_143_out, D6, T4, not_159_out, not_160_out, IR10);
  and and_144 (and_144_out, D6, T4, IR4, not_161_out, IR10);
  and and_145 (and_145_out, D9, T4, not_162_out, not_163_out, not_164_out);
  and and_146 (and_146_out, D9, T5, not_165_out, IR7, IR10);
  and and_147 (and_147_out, D9, T4, not_166_out, not_167_out, IR10);
  and and_148 (and_148_out, D9, T4, IR4, not_168_out, IR10);
  and and_149 (and_149_out, D10, T4, not_169_out, not_170_out, not_171_out);
  and and_150 (and_150_out, D10, T5, not_172_out, IR7, IR10);
  and and_151 (and_151_out, D10, T4, not_173_out, not_174_out, IR10);
  and and_152 (and_152_out, D10, T4, IR4, not_175_out, IR10);
  and and_153 (and_153_out, D11, T4, not_176_out, not_177_out);
  and and_154 (and_154_out, D11, T4, not_178_out, IR10);
  and and_155 (and_155_out, D11, T4, IR7, IR10);
  and and_156 (and_156_out, D12, T4, not_179_out, not_180_out);
  and and_157 (and_157_out, D12, T4, not_181_out, IR10);
  and and_158 (and_158_out, D12, T4, IR7, IR10);
  and and_159 (and_159_out, D13, T4, not_182_out, not_183_out);
  and and_160 (and_160_out, D13, T4, not_184_out, IR10);
  and and_161 (and_161_out, D13, T4, IR7, IR10);
  or or_33 (or_33_out, and_137_out, and_138_out, and_139_out, and_140_out);
  or or_34 (or_34_out, and_153_out, and_154_out);
  or or_35 (or_35_out, and_156_out, and_157_out, and_158_out);
  or or_36 (or_36_out, and_159_out, and_160_out, and_161_out);
  or or_37 (or_37_out, and_131_out, and_132_out, and_133_out, and_134_out, and_135_out, and_136_out);
  or or_38 (or_38_out, and_141_out, and_142_out, and_143_out, and_144_out);
  or or_39 (or_39_out, and_145_out, and_146_out, and_147_out, and_148_out);
  or or_40 (or_40_out, and_149_out, and_150_out, and_151_out, and_152_out);
  assign FunSelALU = or_37_out ? 4'b0000 : 4'bz;  // Controlled_Buffer controlled_buffer_38
  assign FunSelALU = or_33_out ? 4'b0100 : 4'bz;  // Controlled_Buffer controlled_buffer_39
  assign FunSelALU = or_38_out ? 4'b0110 : 4'bz;  // Controlled_Buffer controlled_buffer_40
  assign FunSelALU = or_34_out ? 4'b0011 : 4'bz;  // Controlled_Buffer controlled_buffer_41
  assign FunSelALU = and_155_out ? 4'b0010 : 4'bz;  // Controlled_Buffer controlled_buffer_42
  assign FunSelALU = or_35_out ? 4'b1010 : 4'bz;  // Controlled_Buffer controlled_buffer_43
  assign FunSelALU = or_36_out ? 4'b1011 : 4'bz;  // Controlled_Buffer controlled_buffer_44
  assign FunSelALU = or_39_out ? 4'b0111 : 4'bz;  // Controlled_Buffer controlled_buffer_45
  assign FunSelALU = or_40_out ? 4'b1000 : 4'bz;  // Controlled_Buffer controlled_buffer_46
  or or_41 (or_41_out, T0, T2);
  assign FunSelIR = or_41_out ? 2'b11 : 2'bz;  // Controlled_Buffer controlled_buffer_47
  assign L_H = T0 ? 1'b1 : 1'bz;  // Controlled_Buffer controlled_buffer_48
  assign L_H = T2 ? 1'b0 : 1'bz;  // Controlled_Buffer controlled_buffer_49
  and and_162 (and_162_out, D0, T5);
  and and_163 (and_163_out, D4, T5);
  and and_164 (and_164_out, D18, T5);
  or or_42 (or_42_out, T0, T2, and_162_out, and_163_out, and_164_out);
  assign Load = or_42_out ? 1'b1 : 1'bz;  // Controlled_Buffer controlled_buffer_50
  not not_185 (not_185_out, or_42_out);
  assign Load = not_185_out ? 1'b0 : 1'bz;  // Controlled_Buffer controlled_buffer_51
  not not_186 (not_186_out, IR8);
  not not_187 (not_187_out, IR10);
  not not_188 (not_188_out, IR4);
  not not_189 (not_189_out, IR7);
  not not_190 (not_190_out, IR10);
  not not_191 (not_191_out, IR4);
  not not_192 (not_192_out, IR10);
  not not_193 (not_193_out, IR7);
  not not_194 (not_194_out, IR10);
  not not_195 (not_195_out, IR4);
  not not_196 (not_196_out, IR7);
  not not_197 (not_197_out, IR4);
  not not_198 (not_198_out, IR7);
  not not_199 (not_199_out, IR10);
  not not_200 (not_200_out, IR7);
  not not_201 (not_201_out, IR10);
  not not_202 (not_202_out, IR7);
  not not_203 (not_203_out, SRC__DEST);
  not not_204 (not_204_out, SRC__DEST);
  not not_205 (not_205_out, IR10);
  not not_206 (not_206_out, IR7);
  and and_165 (and_165_out, D2_D5_D9_D10_D11_D12_D13_D14_D15_D16, T4);
  and and_166 (and_166_out, D1_D3_D4_D18, T5);
  and and_167 (and_167_out, D17, T6);
  and and_168 (and_168_out, D0, T4, not_186_out);
  and and_169 (and_169_out, D0, T5, IR8);
  and and_170 (and_170_out, D6, T4, not_187_out, not_188_out, not_189_out);
  and and_171 (and_171_out, D6, T4, not_190_out, not_191_out, IR7);
  and and_172 (and_172_out, D6, T5, not_192_out, IR4, not_193_out);
  and and_173 (and_173_out, D6, T4, not_194_out, IR4, IR7);
  and and_174 (and_174_out, D6, T4, IR10, not_195_out, not_196_out);
  and and_175 (and_175_out, D6, T4, IR10, not_197_out, IR7);
  and and_176 (and_176_out, D6, T4, IR10, IR4, not_198_out);
  and and_177 (and_177_out, D6, T4, IR10, IR4, IR7);
  and and_178 (and_178_out, D7_D8, T5, not_199_out, not_200_out, SRC__DEST);
  and and_179 (and_179_out, D7_D8, T5, not_201_out, not_202_out, not_203_out);
  and and_180 (and_180_out, D7_D8, T5, IR10, IR7, SRC__DEST);
  and and_181 (and_181_out, D7_D8, T5, IR10, IR7, not_204_out);
  and and_182 (and_182_out, D7_D8, T6, not_205_out, IR7);
  and and_183 (and_183_out, D7_D8, T6, IR10, not_206_out);
  or or_43 (or_43_out, T0, T2);
  assign En = or_43_out ? 1'b1 : 1'bz;  // Controlled_Buffer controlled_buffer_52
  and and_184 (and_184_out, D3, T4);
  and and_185 (and_185_out, D1, T5);
  and and_186 (and_186_out, D17, T4);
  or or_44 (or_44_out, and_185_out, and_184_out, and_186_out);
  assign Store = or_44_out ? 1'b1 : 1'bz;  // Controlled_Buffer controlled_buffer_53
  not not_207 (not_207_out, or_44_out);
  assign Store = not_207_out ? 1'b0 : 1'bz;  // Controlled_Buffer controlled_buffer_54
  or or_45 (or_45_out, and_165_out, and_166_out, and_167_out, and_168_out, and_169_out, and_170_out, and_171_out, and_172_out, and_173_out, and_174_out, and_175_out, and_176_out, and_177_out, and_178_out, and_179_out, and_180_out, and_181_out, and_182_out, and_183_out);
  assign SC_Clear = or_45_out ? 1'b1 : 1'bz;  // Controlled_Buffer controlled_buffer_55
  not not_208 (not_208_out, or_45_out);
  assign SC_Clear = not_208_out ? 1'b0 : 1'bz;  // Controlled_Buffer controlled_buffer_56
  Clock CLK (.out(CLK_out));
  or or_46 (D1_D3_D4_D18, D18, D4, D3, D1);
  xnor xnor_1 (xnor_1_out, IR5, IR8);
  and and_187 (SRC__DEST, xnor_1_out, xnor_2_out);
  xnor xnor_2 (xnor_2_out, IR6, IR9);
  Counter #(.width(3), .max('h7)) counter_1 (
    .Q(counter_1_q), .clk(CLK_out), .clr(d_ff_1_q));  // open: load, D, count, carry
  Decoder #(.select(3)) decoder_1 (
    .out0(T0), .out1(T1), .out2(T2), .out3(T3), .out4(T4), .out5(T5), .out6(T6), .sel(counter_1_q));  // open: out7, en
  D_Flip_Flop d_ff_1 (.clk(CLK_out), .D(SC_Clear), .Q(d_ff_1_q));  // open: Qn, preset, en, reset
  or or_47 (D7_D8, D8, D7);
  or or_48 (D5_D6_D9_D10, D10, D9, D6, D5);
  or or_49 (D2_D11_D12_D13, D13, D12, D11, D2);
  or or_50 (D5_D6_D9_D10, D5, D6, D9, D10);
  or or_51 (D0_D4, D4, D0);
  or or_52 (D5_D9_D10, D10, D9, D5);
  or or_53 (D9_D10, D10, D9);
  or or_54 (D2_D12_D13, D13, D12, D2);
  proj2part2_main main_1 (
    .MuxCSel(MuxCSel), .OutASel(OutASel), .OutBSel(OutBSel), .RegSelRF(RegSelRF), .FunSelALU(FunSelALU),
    .FunSelRF(FunSelRF), .CLK(CLK_out), .MuxASel(MuxASel), .FunSelARF(FunSelARF), .RegSelARF(RegSelARF),
    .Store(Store), .L_H(L_H), .En(En), .FunSelIR(FunSelIR), .MuxBSel(MuxBSel), .OutCsel(OutCSel),
    .OutDsel(OutDSel), .Z(Z), .Load(Load),
    .Instruction({IR15, IR14, IR13, IR12, IR11, IR10, IR9, IR8, IR7, IR6, IR5, IR4, IR3, IR2, IR1, IR0}));
  Decoder #(.select(5)) decoder_2 (
    .out0(D0), .out1(D1), .out2(D2), .out3(D3), .out4(D4), .out5(D5), .out6(D6), .out7(D7), .out8(D8),
    .out9(D9), .out10(D10), .out11(D11), .out12(D12), .out13(D13), .out14(D14), .out15(D15), .out16(D14),
    .out17(D15), .out18(D16), .out19(D17), .out20(D18), .sel({IR15, IR14, IR13, IR12, IR11}));  // open: out21, out22, out23, out24, out25, out26, out27, out28, out29, out30, out31, en
  or or_55 (D11_D12_D13, D13, D12, D11);
  or or_56 (D7_D8, D7, D8);
  or or_57 (D2_D5_D9_D10_D11_D12_D13_D14_D15_D16, D2, D16, D15, D14, D5, D9, D10, D11, D12, D13);
endmodule

module RFDecoder (
  input  [1:0] Input,
  output [3:0] Output
);

  Multiplexer #(.select(2), .width(4)) multiplexer_1 (
    .in0(4'b0001), .in1(4'b0010), .in2(4'b0100), .in3(4'b1000), .out(Output), .sel(Input));  // open: en
endmodule

module ARFDecoder (
  input  [1:0] Input,
  output [2:0] Output
);

  Multiplexer #(.select(2), .width(3)) multiplexer_1 (
    .in0(3'b001), .in1(3'b001), .in2(3'b010), .in3(3'b100), .out(Output), .sel(Input));  // open: en
endmodule
