// Logisim project 8bit.circ as structural Verilog: 2 circuits, main circuit main
module main (
  input  [7:0] Input,
  input  [1:0] FunSel,
  input  Enable,
  output [7:0] Output
);

  wire CLK_out;

  Hex_Digit_Display hex_digit_display_1 (.value(Input[7:4]));  // open: dp
  Clock CLK (.out(CLK_out));
  Hex_Digit_Display hex_digit_display_2 (.value(Input[3:0]));  // open: dp
  _8_bit u_8_bit_1 (.Input(Input), .FunSel(FunSel), .CLK(CLK_out), .Enable(Enable), .Output(Output));
  Hex_Digit_Display hex_digit_display_3 (.value(Output[7:4]));  // open: dp
  Hex_Digit_Display hex_digit_display_4 (.value(Output[3:0]));  // open: dp
endmodule

module _8_bit (
  input  [7:0] Input,
  input  [1:0] FunSel,
  input  CLK,
  input  Enable,
  output [7:0] Output
);

  wire adder_1_cout, adder_1_out, adder_2_cout, adder_2_out, adder_3_cout, adder_3_out, adder_4_cout,
       adder_4_out, adder_5_cout, adder_5_out, adder_6_cout, adder_6_out, adder_7_cout, adder_7_out,
       adder_8_out, multiplexer_1_out, multiplexer_2_out, multiplexer_3_out, multiplexer_4_out,
       multiplexer_5_out, multiplexer_6_out, multiplexer_7_out, multiplexer_8_out, not_1_out,
       subtractor_1_bout, subtractor_1_out, subtractor_2_bout, subtractor_2_out, subtractor_3_bout,
       subtractor_3_out, subtractor_4_bout, subtractor_4_out, subtractor_5_bout, subtractor_5_out,
       subtractor_6_bout, subtractor_6_out, subtractor_7_bout, subtractor_7_out, subtractor_8_out;

  Multiplexer #(.select(2), .enable("false")) multiplexer_1 (
    .in0(not_1_out), .in1(Input[0]), .in2(adder_1_out), .in3(subtractor_1_out), .out(multiplexer_1_out),
    .sel(FunSel));
  not not_1 (not_1_out, Enable);
  Adder #(.width(1)) adder_1 (.a(Output[0]), .b(Enable), .out(adder_1_out), .cout(adder_1_cout));  // open: cin
  Subtractor #(.width(1)) subtractor_1 (
    .a(Output[0]), .b(Enable), .out(subtractor_1_out), .bout(subtractor_1_bout));  // open: bin
  D_Flip_Flop d_ff_1 (.clk(CLK), .D(multiplexer_1_out), .Q(Output[0]), .en(Enable));  // open: Qn, preset, reset
  Multiplexer #(.select(2), .enable("false")) multiplexer_2 (
    .in0(not_1_out), .in1(Input[1]), .in2(adder_2_out), .in3(subtractor_2_out), .out(multiplexer_2_out),
    .sel(FunSel));
  D_Flip_Flop d_ff_2 (.clk(CLK), .D(multiplexer_2_out), .Q(Output[1]), .en(Enable));  // open: Qn, preset, reset
  Adder #(.width(1)) adder_2 (.a(Output[1]), .b(adder_1_cout), .out(adder_2_out), .cout(adder_2_cout));  // open: cin
  Subtractor #(.width(1)) subtractor_2 (
    .a(Output[1]), .b(subtractor_1_bout), .out(subtractor_2_out), .bout(subtractor_2_bout));  // open: bin
  Multiplexer #(.select(2), .enable("false")) multiplexer_3 (
    .in0(not_1_out), .in1(Input[2]), .in2(adder_3_out), .in3(subtractor_3_out), .out(multiplexer_3_out),
    .sel(FunSel));
  D_Flip_Flop d_ff_3 (.clk(CLK), .D(multiplexer_3_out), .Q(Output[2]), .en(Enable));  // open: Qn, preset, reset
  Adder #(.width(1)) adder_3 (.a(Output[2]), .b(adder_2_cout), .out(adder_3_out), .cout(adder_3_cout));  // open: cin
  Subtractor #(.width(1)) subtractor_3 (
    .a(Output[2]), .b(subtractor_2_bout), .out(subtractor_3_out), .bout(subtractor_3_bout));  // open: bin
  Multiplexer #(.select(2), .enable("false")) multiplexer_4 (
    .in0(not_1_out), .in1(Input[3]), .in2(adder_4_out), .in3(subtractor_4_out), .out(multiplexer_4_out),
    .sel(FunSel));
  D_Flip_Flop d_ff_4 (.clk(CLK), .D(multiplexer_4_out), .Q(Output[3]), .en(Enable));  // open: Qn, preset, reset
  Adder #(.width(1)) adder_4 (.a(Output[3]), .b(adder_3_cout), .out(adder_4_out), .cout(adder_4_cout));  // open: cin
  Subtractor #(.width(1)) subtractor_4 (
    .a(Output[3]), .b(subtractor_3_bout), .out(subtractor_4_out), .bout(subtractor_4_bout));  // open: bin
  Multiplexer #(.select(2), .enable("false")) multiplexer_5 (
    .in0(not_1_out), .in1(Input[4]), .in2(adder_5_out), .in3(subtractor_5_out), .out(multiplexer_5_out),
    .sel(FunSel));
  D_Flip_Flop d_ff_5 (.clk(CLK), .D(multiplexer_5_out), .Q(Output[4]), .en(Enable));  // open: Qn, preset, reset
  Adder #(.width(1)) adder_5 (.a(Output[4]), .b(adder_4_cout), .out(adder_5_out), .cout(adder_5_cout));  // open: cin
  Subtractor #(.width(1)) subtractor_5 (
    .a(Output[4]), .b(subtractor_4_bout), .out(subtractor_5_out), .bout(subtractor_5_bout));  // open: bin
  Multiplexer #(.select(2), .enable("false")) multiplexer_6 (
    .in0(not_1_out), .in1(Input[5]), .in2(adder_6_out), .in3(subtractor_6_out), .out(multiplexer_6_out),
    .sel(FunSel));
  D_Flip_Flop d_ff_6 (.clk(CLK), .D(multiplexer_6_out), .Q(Output[5]), .en(Enable));  // open: Qn, preset, reset
  Adder #(.width(1)) adder_6 (.a(Output[5]), .b(adder_5_cout), .out(adder_6_out), .cout(adder_6_cout));  // open: cin
  Subtractor #(.width(1)) subtractor_6 (
    .a(Output[5]), .b(subtractor_5_bout), .out(subtractor_6_out), .bout(subtractor_6_bout));  // open: bin
  Multiplexer #(.select(2), .enable("false")) multiplexer_7 (
    .in0(not_1_out), .in1(Input[6]), .in2(adder_7_out), .in3(subtractor_7_out), .out(multiplexer_7_out),
    .sel(FunSel));
  D_Flip_Flop d_ff_7 (.clk(CLK), .D(multiplexer_7_out), .Q(Output[6]), .en(Enable));  // open: Qn, preset, reset
  Adder #(.width(1)) adder_7 (.a(Output[6]), .b(adder_6_cout), .out(adder_7_out), .cout(adder_7_cout));  // open: cin
  Subtractor #(.width(1)) subtractor_7 (
    .a(Output[6]), .b(subtractor_6_bout), .out(subtractor_7_out), .bout(subtractor_7_bout));  // open: bin
  Multiplexer #(.select(2), .enable("false")) multiplexer_8 (
    .in0(not_1_out), .in1(Input[7]), .in2(adder_8_out), .in3(subtractor_8_out), .out(multiplexer_8_out),
    .sel(FunSel));
  D_Flip_Flop d_ff_8 (.clk(CLK), .D(multiplexer_8_out), .Q(Output[7]), .en(Enable));  // open: Qn, preset, reset
  Adder #(.width(1)) adder_8 (.a(Output[7]), .b(adder_7_cout), .out(adder_8_out));  // open: cin, cout
  Subtractor #(.width(1)) subtractor_8 (
    .a(Output[7]), .b(subtractor_7_bout), .out(subtractor_8_out));  // open: bin, bout
endmodule
