// Logisim project proj1part2c.circ as structural Verilog: 2 circuits, main circuit main
module main (
  input  [7:0] Input,
  input  L_H,
  input  En,
  input  [1:0] FunSel
);

  wire CLK_out;
  wire [15:0] n2c_1_output;

  Hex_Digit_Display hex_digit_display_1 (.value(Input[3:0]));  // open: dp
  Hex_Digit_Display hex_digit_display_2 (.value(Input[7:4]));  // open: dp
  Clock CLK (.out(CLK_out));
  _2c u_2c_1 (.Input(Input), .L_H(L_H), .CLK(CLK_out), .En(En), .FunSel(FunSel), .Output(n2c_1_output));
  Hex_Digit_Display hex_digit_display_3 (.value(n2c_1_output[15:12]));  // open: dp
  Hex_Digit_Display hex_digit_display_4 (.value(n2c_1_output[11:8]));  // open: dp
  Hex_Digit_Display hex_digit_display_5 (.value(n2c_1_output[3:0]));  // open: dp
  Hex_Digit_Display hex_digit_display_6 (.value(n2c_1_output[7:4]));  // open: dp
endmodule

module _2c (
  input  [7:0] Input,
  input  L_H,
  input  CLK,
  input  En,
  input  [1:0] FunSel,
  output [15:0] Output
);

  wire [0:0] not_1_out;
  wire [1:0] multiplexer_5_out, not_3_out;
  wire [1:1] not_2_out;
  wire [15:0] multiplexer_1_out;

  Hex_Digit_Display hex_digit_display_1 (.value(Input[7:4]));  // open: dp
  Hex_Digit_Display hex_digit_display_2 (.value(Input[3:0]));  // open: dp
  Multiplexer #(.enable("false")) multiplexer_1 (
    .in0(Input[0]), .in1(Output[0]), .out(multiplexer_1_out[0]), .sel(L_H));
  not not_1 (not_1_out[0], FunSel[0]);
  not not_2 (not_2_out[1], FunSel[1]);
  Multiplexer #(.enable("false")) multiplexer_2 (
    .in0(Input[1]), .in1(Output[1]), .out(multiplexer_1_out[1]), .sel(L_H));
  assign not_3_out = ~FunSel;  // NOT_Gate not_3, 2 bits wide
  Multiplexer #(.enable("false")) multiplexer_3 (
    .in0(Input[3]), .in1(Output[3]), .out(multiplexer_1_out[3]), .sel(L_H));
  Multiplexer #(.enable("false")) multiplexer_4 (
    .in0(Input[2]), .in1(Output[2]), .out(multiplexer_1_out[2]), .sel(L_H));
  Multiplexer #(.select(2), .width(2), .enable("false")) multiplexer_5 (
    .in0(FunSel), .in1(not_3_out), .in2({FunSel[1], not_1_out[0]}), .in3({not_2_out[1], FunSel[0]}),
    .out(multiplexer_5_out), .sel(FunSel));
  Multiplexer #(.enable("false")) multiplexer_6 (
    .in0(Input[4]), .in1(Output[4]), .out(multiplexer_1_out[4]), .sel(L_H));
  Multiplexer #(.enable("false")) multiplexer_7 (
    .in0(Input[5]), .in1(Output[5]), .out(multiplexer_1_out[5]), .sel(L_H));
  Multiplexer #(.enable("false")) multiplexer_8 (
    .in0(Input[6]), .in1(Output[6]), .out(multiplexer_1_out[6]), .sel(L_H));
  Multiplexer #(.enable("false")) multiplexer_9 (
    .in0(Input[7]), .in1(Output[7]), .out(multiplexer_1_out[7]), .sel(L_H));
  Multiplexer #(.enable("false")) multiplexer_10 (
    .in0(Output[8]), .in1(Input[0]), .out(multiplexer_1_out[8]), .sel(L_H));
  Multiplexer #(.enable("false")) multiplexer_11 (
    .in0(Output[9]), .in1(Input[1]), .out(multiplexer_1_out[9]), .sel(L_H));
  _16bit u_16bit_1 (.FunSel(multiplexer_5_out), .CLK(CLK), .Enable(En), .Input(multiplexer_1_out), .Output(Output));
  Multiplexer #(.enable("false")) multiplexer_12 (
    .in0(Output[10]), .in1(Input[2]), .out(multiplexer_1_out[10]), .sel(L_H));
  Multiplexer #(.enable("false")) multiplexer_13 (
    .in0(Output[11]), .in1(Input[3]), .out(multiplexer_1_out[11]), .sel(L_H));
  Multiplexer #(.enable("false")) multiplexer_14 (
    .in0(Output[13]), .in1(Input[5]), .out(multiplexer_1_out[13]), .sel(L_H));
  Multiplexer #(.enable("false")) multiplexer_15 (
    .in0(Output[12]), .in1(Input[4]), .out(multiplexer_1_out[12]), .sel(L_H));
  Multiplexer #(.enable("false")) multiplexer_16 (
    .in0(Output[14]), .in1(Input[6]), .out(multiplexer_1_out[14]), .sel(L_H));
  Multiplexer #(.enable("false")) multiplexer_17 (
    .in0(Output[15]), .in1(Input[7]), .out(multiplexer_1_out[15]), .sel(L_H));
endmodule
