// Logisim project proj2part2.circ as structural Verilog: 1 circuit, main circuit main
module main (
  input  MuxCSel,
  input  [1:0] OutASel,
  input  [1:0] OutBSel,
  input  [3:0] RegSelRF,
  input  [3:0] FunSelALU,
  input  [1:0] FunSelRF,
  input  CLK,
  input  [1:0] MuxASel,
  input  [1:0] FunSelARF,
  input  [1:0] MuxBSel,
  input  [2:0] RegSelARF,
  input  [1:0] OutCsel,
  input  [1:0] OutDsel,
  input  Store,
  input  Load,
  input  L_H,
  input  En,
  input  [1:0] FunSelIR,
  output Z,
  output [15:0] Instruction
);

  wire C_output;
  wire [3:0] ALU_outflag;
  wire [7:0] ALU_outalu, ARF_p7, ARF_p8, multiplexer_1_out, multiplexer_2_out, multiplexer_3_out, ram_1_data,
       RF_outa, RF_outb;

  Multiplexer #(.select(2), .width(8)) multiplexer_1 (
    .in0(Instruction[7:0]), .in1(ram_1_data), .in2(ARF_p7), .in3(ALU_outalu), .out(multiplexer_1_out),
    .sel(MuxASel));  // open: en
  _2c IR (.Input(ram_1_data), .L_H(L_H), .CLK(CLK), .En(En), .FunSel(FunSelIR), .Output(Instruction));
  _2a RF (
    .Input(multiplexer_1_out), .OutASel(OutASel), .OutBSel(OutBSel), .RegSel(RegSelRF), .FunSel(FunSelRF),
    .CLK(CLK), .OutA(RF_outa), .OutB(RF_outb));
  Multiplexer #(.width(8)) multiplexer_2 (
    .in0(ARF_p7), .in1(RF_outa), .out(multiplexer_2_out), .sel(MuxCSel));  // open: en
  Multiplexer #(.select(2), .width(8)) multiplexer_3 (
    .in1(Instruction[7:0]), .in2(ram_1_data), .in3(ALU_outalu), .out(multiplexer_3_out), .sel(MuxBSel));  // open: in0, en
  Hex_Digit_Display hex_digit_display_1 (.value(Instruction[15:12]));  // open: dp
  Hex_Digit_Display hex_digit_display_2 (.value(Instruction[7:4]));  // open: dp
  Hex_Digit_Display hex_digit_display_3 (.value(Instruction[11:8]));  // open: dp
  Hex_Digit_Display hex_digit_display_4 (.value(Instruction[3:0]));  // open: dp
  ALU ALU (
    .A(multiplexer_2_out), .B(RF_outb), .Carry_In(C_output), .FunSel(FunSelALU), .OutALU(ALU_outalu),
    .OutFlag(ALU_outflag));
  // _2b ARF: pin names not known; wires that end beside it: multiplexer_3_out, FunSelARF, CLK, RegSelARF, OutCsel, OutDsel, ARF_p7, ARF_p8
  FR u_Z (.CLK(CLK), .Input(ALU_outflag[3]), .Output(Z));
  FR C (.CLK(CLK), .Input(ALU_outflag[2]), .Output(C_output));
  FR N (.CLK(CLK), .Input(ALU_outflag[1]));  // open: Output
  FR O (.CLK(CLK), .Input(ALU_outflag[0]));  // open: Output
  RAM #(.bus("separate")) ram_1 (
    .addr(ARF_p8), .din(ALU_outalu), .data(ram_1_data), .str(Store), .clk(CLK), .ld(Load));  // open: sel, clr

  // Notes on the sheet:
  //   A
  //   C
  //   B
endmodule
